// Logisim project Projeto somador-subtrator.circ as structural Verilog: 7 circuits, main circuit main
module main (
  input  Sinal_A,
  input  in_2,
  input  in_3,
  input  in_4,
  input  in_5,
  input  in_6,
  input  in_7,
  input  \Operação ,
  input  Sinal_B,
  input  in_10,
  input  in_11,
  input  in_12,
  input  in_13,
  input  in_14,
  input  in_15
);

  wire Operador_lsb_3, Operador_msb_3, Operador_out_17, Operador_out_18, Operador_out_19, Operador_out_20,
       OVF, S1, S2, S3, S4, S5, S6, TOTAL;

  _7_Segment_Display u_7_segment_display_1 (.g(Sinal_A));  // open: f, a, b, e, d, c, dp
  Hex_Digit_Display hex_digit_display_1 (.value({2'b00, in_2, in_3}));  // open: dp
  Hex_Digit_Display hex_digit_display_2 (.value({in_4, in_5, in_6, in_7}));  // open: dp
  _7_Segment_Display u_7_segment_display_2 (.g(\Operação ), .b(\Operação ), .c(\Operação ));  // open: f, a, e, d, dp
  _7_Segment_Display u_7_segment_display_3 (.g(1'b1));  // open: f, a, b, e, d, c, dp
  _7_Segment_Display u_7_segment_display_4 (.g(Sinal_B));  // open: f, a, b, e, d, c, dp
  Hex_Digit_Display hex_digit_display_3 (.value({2'b00, in_10, in_11}));  // open: dp
  Complemento Complemento (
    .LSB(Operador_lsb_3), .in_2(Operador_out_17), .in_3(Operador_out_18), .in_4(Operador_out_19),
    .in_5(Operador_out_20), .MSB(Operador_msb_3), .in_7(TOTAL), .LSB_2(S1), .out_9(S2), .out_10(S3),
    .out_11(S4), .out_12(S5), .MSB_2(S6));
  Somador_circ Operador (
    .LSB(in_7), .in_5(in_6), .in_7(in_5), .in_9(in_4), .in_11(in_3), .MSB(in_2), .OVF(OVF),
    .LSB_3(Operador_lsb_3), .out_17(Operador_out_17), .out_18(Operador_out_18), .out_19(Operador_out_19),
    .out_20(Operador_out_20), .MSB_3(Operador_msb_3), .in_1(Sinal_A), .in_2(Sinal_B), .LSB_2(in_15),
    .in_6(in_14), .in_8(in_13), .in_10(in_12), .in_12(in_11), .MSB_2(in_10), .in_15(\Operação ));
  Hex_Digit_Display hex_digit_display_4 (.value({in_12, in_13, in_14, in_15}));  // open: dp
  _7_Segment_Display u_7_segment_display_5 (.g(TOTAL));  // open: f, a, b, e, d, c, dp
  Hex_Digit_Display hex_digit_display_5 (.value({2'b00, S6, S5}));  // open: dp
  Hex_Digit_Display hex_digit_display_6 (.value({S4, S3, S2, S1}));  // open: dp
  LED Overflow (.in(OVF));
  Inversor_sinal Verificador (
    .A_LSB(in_7), .B_LSB(in_15), .in_3(in_6), .in_4(in_14), .in_5(in_5), .in_6(in_13), .in_7(in_4),
    .in_8(in_12), .in_9(in_3), .in_10(in_11), .A_MSB(in_2), .B_MSB(in_10), .minus_A(Sinal_A),
    .minus_B(Sinal_B), .\Expressão (\Operação ), .out_16(TOTAL));

  // Other names for the same wires on the sheet: A5 = in_3; A6 = in_2; A1 = in_7; A2 = in_6; A3 = in_5; A4 = in_4;
  //   B5 = in_11; B6 = in_10; B1 = in_15; B2 = in_14; B3 = in_13; B4 = in_12; minus_A = Sinal_A; minus_B = Sinal_B;
  //   SoSu = \Operação 

  // Notes on the sheet:
  //   =
endmodule

module Somador_circ (
  input  in_1,
  input  in_2,
  input  LSB,
  input  LSB_2,
  input  in_5,
  input  in_6,
  input  in_7,
  input  in_8,
  input  in_9,
  input  in_10,
  input  in_11,
  input  in_12,
  input  MSB,
  input  MSB_2,
  input  in_15,
  output LSB_3,
  output out_17,
  output out_18,
  output out_19,
  output out_20,
  output MSB_3,
  output OVF
);

  wire A1, A2, A3, A4, A5, A6, B1, B2, B3, B4, B5, B6, somador_logi_1_vai_1, somador_logi_2_vai_1,
       somador_logi_3_vai_1, somador_logi_4_vai_1, somador_logi_5_vai_1, somador_logi_6_vai_1;

  Somador_logi somador_logi_1 (
    .A(A1), .B(B1), .CHEGA_1(1'b0), .S(LSB_3), .VAI_1(somador_logi_1_vai_1), .Soma_Sub(in_15));
  Complemento complemento_1 (
    .LSB(LSB), .in_2(in_5), .in_3(in_7), .in_4(in_9), .in_5(in_11), .MSB(MSB), .in_7(in_1), .LSB_2(A1),
    .out_9(A2), .out_10(A3), .out_11(A4), .out_12(A5), .MSB_2(A6));
  Somador_logi somador_logi_2 (
    .A(A2), .B(B2), .CHEGA_1(somador_logi_1_vai_1), .S(out_17), .VAI_1(somador_logi_2_vai_1), .Soma_Sub(in_15));
  Somador_logi somador_logi_3 (
    .A(A3), .B(B3), .CHEGA_1(somador_logi_2_vai_1), .S(out_18), .VAI_1(somador_logi_3_vai_1), .Soma_Sub(in_15));
  Somador_logi somador_logi_4 (
    .A(A4), .B(B4), .CHEGA_1(somador_logi_3_vai_1), .S(out_19), .VAI_1(somador_logi_4_vai_1), .Soma_Sub(in_15));
  Somador_logi somador_logi_5 (
    .A(A5), .B(B5), .CHEGA_1(somador_logi_4_vai_1), .S(out_20), .VAI_1(somador_logi_5_vai_1), .Soma_Sub(in_15));
  Complemento complemento_2 (
    .LSB(LSB_2), .in_2(in_6), .in_3(in_8), .in_4(in_10), .in_5(in_12), .MSB(MSB_2), .in_7(in_2), .LSB_2(B1),
    .out_9(B2), .out_10(B3), .out_11(B4), .out_12(B5), .MSB_2(B6));
  Somador_logi somador_logi_6 (
    .A(A6), .B(B6), .CHEGA_1(somador_logi_5_vai_1), .S(MSB_3), .VAI_1(somador_logi_6_vai_1), .Soma_Sub(in_15));
  xor xor_1 (OVF, somador_logi_6_vai_1, somador_logi_5_vai_1);

  // Other names for the same wires on the sheet: SoSu = in_15
endmodule

module Somador_logi (
  input  A,
  input  B,
  input  CHEGA_1,
  input  Soma_Sub,
  output S,
  output VAI_1
);

  wire not_1_out, not_2_out, P1, P2, P3, xor_1_out, xor_2_out, xor_3_out;

  not not_1 (not_1_out, Soma_Sub);
  not not_2 (not_2_out, Soma_Sub);
  xor xor_1 (xor_1_out, A, B);
  xor xor_2 (xor_2_out, A, not_1_out);
  xor xor_3 (xor_3_out, A, not_2_out);
  xor xor_4 (S, xor_1_out, CHEGA_1);
  and and_1 (P1, xor_2_out, B);
  and and_2 (P2, CHEGA_1, B);
  and and_3 (P3, xor_3_out, CHEGA_1);
  or or_1 (VAI_1, P1, P2, P3);

  // Other names for the same wires on the sheet: C1 = CHEGA_1; SoSu = Soma_Sub
endmodule

module Complemento (
  input  LSB,
  input  in_2,
  input  in_3,
  input  in_4,
  input  in_5,
  input  MSB,
  input  in_7,
  output LSB_2,
  output out_9,
  output out_10,
  output out_11,
  output out_12,
  output MSB_2
);

  wire A1, A2, A3, A4, A5, A6, and_1_out, somador_logi_1_vai_1, somador_logi_2_vai_1, somador_logi_3_vai_1,
       somador_logi_4_vai_1, somador_logi_5_vai_1;

  and and_1 (and_1_out, in_7, in_7);
  xor xor_1 (A1, LSB, and_1_out);
  xor xor_2 (A2, in_2, and_1_out);
  xor xor_3 (A3, in_3, and_1_out);
  xor xor_4 (A4, in_4, and_1_out);
  xor xor_5 (A5, in_5, and_1_out);
  xor xor_6 (A6, MSB, and_1_out);
  Somador_logi somador_logi_1 (
    .A(A1), .B(and_1_out), .CHEGA_1(1'b0), .S(LSB_2), .VAI_1(somador_logi_1_vai_1), .Soma_Sub(1'b1));
  Somador_logi somador_logi_2 (
    .A(A2), .B(1'b0), .CHEGA_1(somador_logi_1_vai_1), .S(out_9), .VAI_1(somador_logi_2_vai_1), .Soma_Sub(1'b1));
  Somador_logi somador_logi_3 (
    .A(A3), .B(1'b0), .CHEGA_1(somador_logi_2_vai_1), .S(out_10), .VAI_1(somador_logi_3_vai_1),
    .Soma_Sub(1'b1));
  Somador_logi somador_logi_4 (
    .A(A4), .B(1'b0), .CHEGA_1(somador_logi_3_vai_1), .S(out_11), .VAI_1(somador_logi_4_vai_1),
    .Soma_Sub(1'b1));
  Somador_logi somador_logi_5 (
    .A(A5), .B(1'b0), .CHEGA_1(somador_logi_4_vai_1), .S(out_12), .VAI_1(somador_logi_5_vai_1),
    .Soma_Sub(1'b1));
  Somador_logi somador_logi_6 (
    .A(A6), .B(1'b0), .CHEGA_1(somador_logi_5_vai_1), .S(MSB_2), .Soma_Sub(1'b1));  // open: VAI_1
endmodule

module Comparador_logi (
  input  in_1,
  input  in_2,
  input  in_3,
  output out_4,
  output out_5,
  output out_6
);

  wire not_1_out, not_2_out, xnor_1_out;

  not not_1 (not_1_out, in_1);
  not not_2 (not_2_out, in_2);
  xnor xnor_1 (xnor_1_out, in_1, in_2);
  and and_1 (out_5, not_1_out, in_2, in_3);
  and and_2 (out_6, in_1, not_2_out, in_3);
  and and_3 (out_4, xnor_1_out, in_3);
endmodule

module Comparador_circ (
  input  MSB,
  input  in_2,
  input  in_3,
  input  in_4,
  input  in_5,
  input  LSB,
  input  MSB_2,
  input  in_8,
  input  in_9,
  input  in_10,
  input  in_11,
  input  LSB_2,
  output out_13,
  output out_14,
  output out_15
);

  wire AF1, AF2, AF3, AF4, AF5, AF6, BF1, BF2, BF3, BF4, BF5, BF6, comparador_logi_2_out_4,
       comparador_logi_3_out_4, comparador_logi_4_out_4, comparador_logi_5_out_4, comparador_logi_6_out_4;

  Comparador_logi comparador_logi_1 (
    .in_1(LSB), .in_2(LSB_2), .in_3(comparador_logi_2_out_4), .out_4(out_13), .out_5(BF1), .out_6(AF1));
  Comparador_logi comparador_logi_2 (
    .in_1(in_5), .in_2(in_11), .in_3(comparador_logi_3_out_4), .out_4(comparador_logi_2_out_4), .out_5(BF2),
    .out_6(AF2));
  Comparador_logi comparador_logi_3 (
    .in_1(in_4), .in_2(in_10), .in_3(comparador_logi_4_out_4), .out_4(comparador_logi_3_out_4), .out_5(BF3),
    .out_6(AF3));
  Comparador_logi comparador_logi_4 (
    .in_1(in_3), .in_2(in_9), .in_3(comparador_logi_5_out_4), .out_4(comparador_logi_4_out_4), .out_5(BF4),
    .out_6(AF4));
  Comparador_logi comparador_logi_5 (
    .in_1(in_2), .in_2(in_8), .in_3(comparador_logi_6_out_4), .out_4(comparador_logi_5_out_4), .out_5(BF5),
    .out_6(AF5));
  Comparador_logi comparador_logi_6 (
    .in_1(MSB), .in_2(MSB_2), .in_3(1'b1), .out_4(comparador_logi_6_out_4), .out_5(BF6), .out_6(AF6));
  or or_1 (out_14, AF1, AF2, AF3, AF4, AF5, AF6);
  or or_2 (out_15, BF1, BF2, BF3, BF4, BF5, BF6);

  // Other names for the same wires on the sheet: A1 = LSB; A2 = in_5; A3 = in_4; A4 = in_3; A5 = in_2; A6 = MSB;
  //   B1 = LSB_2; B2 = in_11; B3 = in_10; B4 = in_9; B5 = in_8; B6 = MSB_2
endmodule

module Inversor_sinal (
  input  A_LSB,
  input  B_LSB,
  input  in_3,
  input  in_4,
  input  in_5,
  input  in_6,
  input  in_7,
  input  in_8,
  input  in_9,
  input  in_10,
  input  A_MSB,
  input  B_MSB,
  input  minus_A,
  input  minus_B,
  input  \Expressão ,
  output out_16
);

  wire A, A_B, and_1_out, and_2_out, and_3_out, and_4_out, B, not_1_out, not_2_out, not_3_out, not_4_out, R1,
       R2;

  not not_1 (not_1_out, minus_B);
  not not_2 (not_2_out, \Expressão );
  not not_3 (not_3_out, minus_B);
  not not_4 (not_4_out, \Expressão );
  and and_1 (and_1_out, B, not_1_out, not_2_out);
  and and_2 (and_2_out, R2, \Expressão );
  and and_3 (and_3_out, A_B, minus_A, not_3_out, not_4_out);
  and and_4 (and_4_out, minus_A, minus_B, \Expressão );
  Comparador_circ comparador_circ_1 (
    .out_13(A_B), .out_14(A), .out_15(B), .MSB(A_MSB), .MSB_2(B_MSB), .in_2(in_9), .in_8(in_10), .in_3(in_7),
    .in_9(in_8), .in_4(in_5), .in_10(in_6), .in_5(in_3), .in_11(in_4), .LSB(A_LSB), .LSB_2(B_LSB));
  or or_1 (out_16, R1, and_1_out, and_2_out, and_3_out, and_4_out);
  and and_5 (R1, minus_A, A);
  and and_6 (R2, minus_B, B);

  // Other names for the same wires on the sheet: A1 = A_LSB; A2 = in_3; A3 = in_5; A4 = in_7; A5 = in_9; A6 = A_MSB;
  //   B1 = B_LSB; B2 = in_4; B3 = in_6; B4 = in_8; B5 = in_10; B6 = B_MSB; EX = \Expressão 
endmodule
