// Logisim project Projeto computador-JoaoAraujo.circ as structural Verilog: 6 circuits, main circuit main
module main (
  output [4:0] out_1
);

  wire ADD, bitselector_1_out, Clear, Clock, Clock_out, EQ, GEQ, GT, HLT, JMP, LEQ, LT, MOVA, MOVY, MUL,
       not_1_out, Pulo, RDM, STR, SUB;
  wire [1:0] controlled_buffer_1_out, Rx, Ry;
  wire [3:0] \Instrução ;
  wire [4:0] Loop;
  wire [7:0] EntraRAM, SaidaRAM, SaidaROM, SaidaRX, SaidaRY, SaiRA, ValorRA;

  Clock u_Clock (.out(Clock_out));
  Button u_Clear (.out(Clear));
  and and_1 (Clock, Clock_out, ~HLT);  // AND_Gate
  ROM #(.addrWidth(5)) rom_1 (.addr(out_1), .data(SaidaROM));  // open: sel
  \Registrador_de_instrução  \registrador_de_instrução_1  (
    .in_1(SaidaROM), .in_2(Clock), .in_3(Clear), .Ry(Ry), .Rx(Rx), .Comando(\Instrução ));
  \Decodificador_de_instrução  \decodificador_de_instrução_1  (
    .in_1(\Instrução ), .out_2(MUL), .out_3(EQ), .out_4(ADD), .out_5(LT), .out_6(SUB), .out_7(GT),
    .out_8(MOVY), .out_9(LEQ), .out_10(MOVA), .out_12(RDM), .out_13(JMP), .out_14(STR), .out_15(HLT),
    .out_11(GEQ));
  not not_1 (not_1_out, Pulo);
  Contador_de_programa contador_de_programa_1 (
    .JUMP(Pulo), .Entrada(Loop), .Bloqueador(not_1_out), .in_4(Clock), .in_5(Clear), .out_6(out_1));
  assign controlled_buffer_1_out = STR ? Rx : 2'bz;  // Controlled_Buffer controlled_buffer_1
  assign controlled_buffer_1_out = RDM ? Ry : 2'bz;  // Controlled_Buffer controlled_buffer_2
  Banco_de_registradores banco_de_registradores_1 (
    .in_10(SaidaRAM), .\Endereço_RX (Rx), .in_3(Clock), .in_4(Clear), .in_6(MOVY), .in_7(MOVA), .in_9(STR),
    .in_8(RDM), .in_11(SaiRA), .out_12(SaidaRX), .out_15(SaidaRY), .\Endereço_RY (Ry), .out_13(EntraRAM),
    .out_14(Loop), .in_5(Pulo));
  RAM #(.addrWidth(2), .bus("separate")) ram_1 (
    .addr(controlled_buffer_1_out), .din(EntraRAM), .data(SaidaRAM), .str(STR), .clk(Clock), .ld(RDM));  // open: sel, clr
  Register #(.trigger("falling")) RA (.D(ValorRA), .Q(SaiRA), .clk(Clock), .clr(Clear));  // open: en
  BitSelector bitselector_1 (.in(SaiRA), .out(bitselector_1_out), .sel(3'b000));
  ALU alu_1 (
    .in_2(SaidaRX), .in_4(SaidaRY), .out_11(ValorRA), .ADD(ADD), .SUB(SUB), .MUL(MUL), .GT(GT), .EQ(EQ),
    .LT(LT), .GEQ(GEQ), .LEQ(LEQ));
  and and_2 (Pulo, JMP, bitselector_1_out);

  // Other names for the same wires on the sheet: PC[4:0] = out_1

  // Notes on the sheet:
  //   ROM
  //   Registrador de instrução
  //   Decodificador de instrução
  //   contents of rom_1 (hex, n*v repeats v):
  //   dd d0 a3 c0 0 4f cc 23 df 7c 0 d9 ef b1 b6 91 c8 dd d0 a3 c0 e0 de 43 c0 df 7c ee f0
  //   Contador de programa
  //   Banco de registradores
  //   RAM
  //   ALU
endmodule

module Contador_de_programa (
  input  JUMP,
  input  [4:0] Entrada,
  input  Bloqueador,
  input  in_4,
  input  in_5,
  output [4:0] out_6
);

  Counter #(.width(5), .max('h1f), .trigger("falling")) counter_1 (
    .load(JUMP), .D(Entrada), .count(Bloqueador), .Q(out_6), .clk(in_4), .clr(in_5));  // open: carry

  // Other names for the same wires on the sheet: Ck = in_4; Clear = in_5
endmodule

module \Registrador_de_instrução  (
  input  [7:0] in_1,
  input  in_2,
  input  in_3,
  output [1:0] Ry,
  output [1:0] Rx,
  output [3:0] Comando
);

  Register #(.trigger("falling")) register_1 (.D(in_1), .Q({Comando, Rx, Ry}), .clk(in_2), .clr(in_3));  // open: en

  // Other names for the same wires on the sheet: Ck = in_2; Clear = in_3; Inst[7:0] = in_1
endmodule

module \Decodificador_de_instrução  (
  input  [3:0] in_1,
  output out_2,
  output out_3,
  output out_4,
  output out_5,
  output out_6,
  output out_7,
  output out_8,
  output out_9,
  output out_10,
  output out_11,
  output out_12,
  output out_13,
  output out_14,
  output out_15
);

  Comparator #(.width(4)) comparator_1 (.a(in_1), .b(4'b0010), .eq(out_3));  // open: gt, lt
  Comparator #(.width(4)) comparator_2 (.a(in_1), .b(4'b0011), .eq(out_5));  // open: gt, lt
  Comparator #(.width(4)) comparator_3 (.a(in_1), .b(4'b0100), .eq(out_7));  // open: gt, lt
  Comparator #(.width(4)) comparator_4 (.a(in_1), .b(4'b0101), .eq(out_9));  // open: gt, lt
  Comparator #(.width(4)) comparator_5 (.a(in_1), .b(4'b0110), .eq(out_11));  // open: gt, lt
  Comparator #(.width(4)) comparator_6 (.a(in_1), .b(4'b0111), .eq(out_13));  // open: gt, lt
  Comparator #(.width(4)) comparator_7 (.a(in_1), .b(4'b1000), .eq(out_2));  // open: gt, lt
  Comparator #(.width(4)) comparator_8 (.a(in_1), .b(4'b1001), .eq(out_4));  // open: gt, lt
  Comparator #(.width(4)) comparator_9 (.a(in_1), .b(4'b1010), .eq(out_6));  // open: gt, lt
  Comparator #(.width(4)) comparator_10 (.a(in_1), .b(4'b1011), .eq(out_8));  // open: gt, lt
  Comparator #(.width(4)) comparator_11 (.a(in_1), .b(4'b1100), .eq(out_10));  // open: gt, lt
  Comparator #(.width(4)) comparator_12 (.a(in_1), .b(4'b1101), .eq(out_12));  // open: gt, lt
  Comparator #(.width(4)) comparator_13 (.a(in_1), .b(4'b1110), .eq(out_14));  // open: gt, lt
  Comparator #(.width(4)) comparator_14 (.a(in_1), .b(4'b1111), .eq(out_15));  // open: gt, lt

  // Other names for the same wires on the sheet: Ent[3:0] = in_1
endmodule

module Banco_de_registradores (
  input  [1:0] \Endereço_RX ,
  input  [1:0] \Endereço_RY ,
  input  in_3,
  input  in_4,
  input  in_5,
  input  in_6,
  input  in_7,
  input  in_8,
  input  in_9,
  input  [7:0] in_10,
  input  [7:0] in_11,
  output [7:0] out_12,
  output [7:0] out_13,
  output [4:0] out_14,
  output [7:0] out_15
);

  wire Cont0, Cont1, Cont2, Cont3, EnD0, EnD1, EnD2, EnD3, EnM0, EnM1, EnM2, EnM3, EnR0, EnR1, EnR2, EnR3,
       Move0, Move1, Move2, Move3, not_1_out, not_2_out, not_3_out, not_4_out, not_5_out, not_6_out,
       not_7_out, not_8_out, Regi0, Regi1, Regi2, Regi3, Regis0, Regis1, Regis2, Regis3;
  wire [7:0] ArmazenaLOOP_out, controlled_buffer_1_out, controlled_buffer_4_out, controlled_buffer_13_out,
       controlled_buffer_16_out, MovendoRX, R0_q, R1_q, R2_q, R3_q;

  not not_1 (not_1_out, \Endereço_RX [0]);
  not not_2 (not_2_out, \Endereço_RX [1]);
  not not_3 (not_3_out, \Endereço_RX [1]);
  not not_4 (not_4_out, \Endereço_RX [0]);
  not not_5 (not_5_out, \Endereço_RY [0]);
  not not_6 (not_6_out, \Endereço_RY [1]);
  not not_7 (not_7_out, \Endereço_RY [1]);
  not not_8 (not_8_out, \Endereço_RY [0]);
  and and_1 (Regi0, not_1_out, not_2_out);
  and and_2 (Regi1, \Endereço_RX [0], not_3_out);
  and and_3 (Regi2, not_4_out, \Endereço_RX [1]);
  and and_4 (Regi3, \Endereço_RX [0], \Endereço_RX [1]);
  and and_5 (Regis0, not_5_out, not_6_out);
  and and_6 (Regis1, \Endereço_RY [0], not_7_out);
  and and_7 (Regis2, not_8_out, \Endereço_RY [1]);
  and and_8 (Regis3, \Endereço_RY [0], \Endereço_RY [1]);
  or or_1 (Cont0, Regis0, Regi0);
  or or_2 (Cont1, Regis1, Regi1);
  or or_3 (Cont2, Regis2, Regi2);
  or or_4 (Cont3, Regis3, Regi3);
  assign controlled_buffer_1_out = EnD0 ? in_10 : 8'bz;  // Controlled_Buffer controlled_buffer_1
  assign controlled_buffer_1_out = EnM0 ? MovendoRX : 8'bz;  // Controlled_Buffer controlled_buffer_2
  assign controlled_buffer_1_out = EnR0 ? in_11 : 8'bz;  // Controlled_Buffer controlled_buffer_3
  assign controlled_buffer_4_out = EnD1 ? in_10 : 8'bz;  // Controlled_Buffer controlled_buffer_4
  assign controlled_buffer_4_out = EnM1 ? MovendoRX : 8'bz;  // Controlled_Buffer controlled_buffer_5
  assign controlled_buffer_4_out = EnR1 ? in_11 : 8'bz;  // Controlled_Buffer controlled_buffer_6
  and and_9 (Move0, Regis0, in_6);
  and and_10 (Move1, Regis1, in_6);
  and and_11 (Move2, Regis2, in_6);
  and and_12 (Move3, Regis3, in_6);
  Register #(.trigger("falling")) R0 (.D(controlled_buffer_1_out), .en(Cont0), .Q(R0_q), .clk(in_3), .clr(in_4));
  Register #(.trigger("falling")) R1 (.D(controlled_buffer_4_out), .en(Cont1), .Q(R1_q), .clk(in_3), .clr(in_4));
  assign out_13 = in_9 ? out_15 : 8'bz;  // Controlled_Buffer ArmazenaRAM
  assign MovendoRX = Move0 ? R0_q : 8'bz;  // Controlled_Buffer controlled_buffer_7
  assign out_12 = Regi0 ? R0_q : 8'bz;  // Controlled_Buffer controlled_buffer_8
  assign out_15 = Regis0 ? R0_q : 8'bz;  // Controlled_Buffer controlled_buffer_9
  assign MovendoRX = Move1 ? R1_q : 8'bz;  // Controlled_Buffer controlled_buffer_10
  assign out_12 = Regi1 ? R1_q : 8'bz;  // Controlled_Buffer controlled_buffer_11
  assign out_15 = Regis1 ? R1_q : 8'bz;  // Controlled_Buffer controlled_buffer_12
  and and_13 (EnD0, Regi0, in_8);
  and and_14 (EnD1, Regi1, in_8);
  and and_15 (EnD2, Regi2, in_8);
  and and_16 (EnD3, Regi3, in_8);
  assign controlled_buffer_13_out = EnD2 ? in_10 : 8'bz;  // Controlled_Buffer controlled_buffer_13
  assign controlled_buffer_13_out = EnM2 ? MovendoRX : 8'bz;  // Controlled_Buffer controlled_buffer_14
  assign controlled_buffer_13_out = EnR2 ? in_11 : 8'bz;  // Controlled_Buffer controlled_buffer_15
  assign controlled_buffer_16_out = EnD3 ? in_10 : 8'bz;  // Controlled_Buffer controlled_buffer_16
  assign controlled_buffer_16_out = EnM3 ? MovendoRX : 8'bz;  // Controlled_Buffer controlled_buffer_17
  assign controlled_buffer_16_out = EnR3 ? in_11 : 8'bz;  // Controlled_Buffer controlled_buffer_18
  and and_17 (EnM0, Regi0, in_6);
  and and_18 (EnM1, Regi1, in_6);
  and and_19 (EnM2, Regi2, in_6);
  and and_20 (EnM3, Regi3, in_6);
  assign ArmazenaLOOP_out = in_5 ? out_12 : 8'bz;  // Controlled_Buffer ArmazenaLOOP
  assign MovendoRX = Move2 ? R2_q : 8'bz;  // Controlled_Buffer controlled_buffer_19
  assign out_12 = Regi2 ? R2_q : 8'bz;  // Controlled_Buffer controlled_buffer_20
  Register #(.trigger("falling")) R2 (.D(controlled_buffer_13_out), .en(Cont2), .Q(R2_q), .clk(in_3), .clr(in_4));
  assign out_15 = Regis2 ? R2_q : 8'bz;  // Controlled_Buffer controlled_buffer_21
  assign MovendoRX = Move3 ? R3_q : 8'bz;  // Controlled_Buffer controlled_buffer_22
  assign out_12 = Regi3 ? R3_q : 8'bz;  // Controlled_Buffer controlled_buffer_23
  Register #(.trigger("falling")) R3 (.D(controlled_buffer_16_out), .en(Cont3), .Q(R3_q), .clk(in_3), .clr(in_4));
  assign out_15 = Regis3 ? R3_q : 8'bz;  // Controlled_Buffer controlled_buffer_24
  and and_21 (EnR0, Regi0, in_7);
  and and_22 (EnR1, Regi1, in_7);
  and and_23 (EnR2, Regi2, in_7);
  and and_24 (EnR3, Regi3, in_7);
  BitSelector #(.group(5)) bitselector_1 (.in(ArmazenaLOOP_out), .out(out_14), .sel(1'b0));

  // Other names for the same wires on the sheet: Ck = in_3; Clear = in_4; Dados[7:0] = in_10; MOVA = in_7;
  //   MOVY = in_6; Pulo = in_5; RA[7:0] = in_11; RDM = in_8; SaidaX[7:0] = out_12; SaidaY[7:0] = out_15; STR = in_9
endmodule

module ALU (
  input  GT,
  input  [7:0] in_2,
  input  EQ,
  input  [7:0] in_4,
  input  LT,
  input  ADD,
  input  GEQ,
  input  SUB,
  input  LEQ,
  input  MUL,
  output [7:0] out_11
);

  wire comparator_1_eq, comparator_1_gt, comparator_1_lt, comparator_2_eq, comparator_2_gt, comparator_2_lt,
       or_1_out, or_2_out;
  wire [7:0] adder_1_out, bitselector_1_out, bitselector_2_out, bitselector_3_out, bitselector_4_out,
       bitselector_5_out, multiplier_1_out, subtractor_1_out;

  Adder adder_1 (.a(in_2), .b(in_4), .out(adder_1_out));  // open: cin, cout
  Subtractor subtractor_1 (.a(in_2), .b(in_4), .out(subtractor_1_out));  // open: bin, bout
  Multiplier multiplier_1 (.a(in_2), .b(in_4), .out(multiplier_1_out));  // open: cin, cout
  assign out_11 = ADD ? adder_1_out : 8'bz;  // Controlled_Buffer controlled_buffer_1
  assign out_11 = SUB ? subtractor_1_out : 8'bz;  // Controlled_Buffer controlled_buffer_2
  assign out_11 = MUL ? multiplier_1_out : 8'bz;  // Controlled_Buffer controlled_buffer_3
  Comparator comparator_1 (.a(in_2), .b(in_4), .gt(comparator_1_gt), .eq(comparator_1_eq), .lt(comparator_1_lt));
  BitSelector #(.width(1), .group(8)) bitselector_1 (.in(comparator_1_gt), .out(bitselector_1_out), .sel(1'b0));
  BitSelector #(.width(1), .group(8)) bitselector_2 (.in(comparator_1_eq), .out(bitselector_2_out), .sel(1'b0));
  BitSelector #(.width(1), .group(8)) bitselector_3 (.in(comparator_1_lt), .out(bitselector_3_out), .sel(1'b0));
  Comparator comparator_2 (.a(in_2), .b(in_4), .gt(comparator_2_gt), .eq(comparator_2_eq), .lt(comparator_2_lt));
  assign out_11 = GT ? bitselector_1_out : 8'bz;  // Controlled_Buffer controlled_buffer_4
  assign out_11 = EQ ? bitselector_2_out : 8'bz;  // Controlled_Buffer controlled_buffer_5
  assign out_11 = LT ? bitselector_3_out : 8'bz;  // Controlled_Buffer controlled_buffer_6
  BitSelector #(.width(1), .group(8)) bitselector_4 (.in(or_1_out), .out(bitselector_4_out), .sel(1'b0));
  or or_1 (or_1_out, comparator_2_gt, comparator_2_eq);
  or or_2 (or_2_out, comparator_2_eq, comparator_2_lt);
  BitSelector #(.width(1), .group(8)) bitselector_5 (.in(or_2_out), .out(bitselector_5_out), .sel(1'b0));
  assign out_11 = GEQ ? bitselector_4_out : 8'bz;  // Controlled_Buffer controlled_buffer_7
  assign out_11 = LEQ ? bitselector_5_out : 8'bz;  // Controlled_Buffer controlled_buffer_8

  // Other names for the same wires on the sheet: FINAL[7:0] = out_11; Valor1[7:0] = in_2; Valor2[7:0] = in_4
endmodule
